# Fritzing sketch UV_TEM (saved by Fritzing 0.9.9b)
circuit board: 8.46667cm x 5.64444cm
breadboards: 1

parts:
  Part1 = Arduino Nano (Rev3.0)
  Part2 = Adafruit AHT20 Temperature and Humidity Sensor [part_number="Adafruit #4566"]
  OLED_I2C1 = OLED 128x64 I2C Monochrome Display
  Part3 = ML8511 Breakout Board

nets:
  GND: Part1.GND, Part2.GND, OLED_I2C1.GND, Part3.GND
  5V: Part1.5V, Part2.VCC, OLED_I2C1.VDD, Part3.VIN
  N1: Part1.A5, Part2.SCL, OLED_I2C1.SCK
  N2: Part1.A4, Part2.SDA, OLED_I2C1.SDA
  N3: Part1.A1, Part3.3V3
  N4: Part1.A0, Part3.OUT
  N5: Part1.3V3, Part3.EN

custom parts:
  Adafruit AHT20 Temperature and Humidity Sensor: The AHT20 is a nice but inexpensive temperature and humidity sensor from the same folks that brought us the DHT22. You can take sensor readings as often as you like, and it uses standard I2C so its super easy to use with any Arduino or Linux/Raspberry Pi board. This sensor has a typical accuracy of +- 2% relative humidity, and +-0.3 °C. There is only one I2C address so its not a good option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
  ML8511 Breakout Board: This breakout board uses the ML8511 UV (ultraviolet) light sensor. The ML8511 works best with light in the 280-390nm wavelengths. The board operates at 2.7 to 3.6V.

// code stored in the sketch: UV_TEP.ino
#include <SPI.h>//
#include <Wire.h>//
#include <Adafruit_GFX.h>//
#include <Adafruit_SSD1306.h>//
#include <Adafruit_AHTX0.h>//
#include <Fonts/FreeSans9pt7b.h>
int UVOUT = A0; //Output from the sensor
int REF_3V3 = A1; //3.3V power on the Arduino board
#define RED 0xF800
#define SCREEN_WIDTH 128 // OLED display width, in pixels
#define SCREEN_HEIGHT 64 // OLED display height, in pixels
#define OLED_RESET     4 // Reset pin # (or -1 if sharing Arduino reset pin)
#define SCREEN_ADDRESS 0x3C ///< See datasheet for Address; 0x3D for 128x64, 0x3C for 128x32
Adafruit_SSD1306 display(SCREEN_WIDTH, SCREEN_HEIGHT, &Wire, OLED_RESET);

Adafruit_AHTX0 aht;
void setup()
{
  Serial.begin(9600);
  pinMode(UVOUT, INPUT);
  pinMode(REF_3V3, INPUT);
  display.begin(SSD1306_SWITCHCAPVCC, 0x3C); //initialize with the I2C addr 0x3C (128x64)
  display.clearDisplay();
  Serial.println("ML8511 example");

// Clear the buffer.
  display.clearDisplay();
  display.display();

  display.setRotation(0); //????
  
  if (aht.begin()) {
    Serial.println("Found AHT20");
  } else {
    Serial.println("Didn't find AHT20");
  }  

  display.setTextSize(1);
  display.setTextColor(SSD1306_WHITE); 
  ///
}

void loop()
{
  int uvLevel = averageAnalogRead(UVOUT);
  int refLevel = averageAnalogRead(REF_3V3);

  //Use the 3.3V power pin as a reference to get a very accurate output value from sensor
  float outputVoltage = 3.3 / refLevel * uvLevel;

  float uvIntensity = mapfloat(outputVoltage, 0.99, 2.8, 0.0, 15.0); //Convert the voltage to a UV intensity level
  sensors_event_t humidity, temp;

  
  display.setCursor(22, 2 ); 
  display.setTextSize(1);
  display.println("UV Ray Intensity");

  display.setCursor(30, 15); //oled display
  display.setTextSize(1);display.println(uvIntensity);

  display.setCursor(60, 15); //oled display
  display.setTextSize(1);display.println("mW/cm^2");



 

  aht.getEvent(&humidity, &temp);// populate temp and humidity objects with fresh data
  display.setCursor(0,25);display.println("Temperature:");
  
  display.setCursor(72,25);display.print(temp.temperature);display.print((char)247);display.print("C");

  display.setCursor(0, 40);display.println("Humidity:");
  display.setCursor(72, 40);display.print(humidity.relative_humidity);display.println("%");



  
  //Serial.print(temp.temperature);
  
  display.display();

  delay(300);
  display.clearDisplay();


}

//Takes an average of readings on a given pin
//Returns the average
int averageAnalogRead(int pinToRead)
{
  byte numberOfReadings = 8;
  unsigned int runningValue = 0;

  for (int x = 0 ; x < numberOfReadings ; x++)
    runningValue += analogRead(pinToRead);
  runningValue /= numberOfReadings;

  return (runningValue);
}

float mapfloat(float x, float in_min, float in_max, float out_min, float out_max)
{
  return (x - in_min) * (out_max - out_min) / (in_max - in_min) + out_min;


}
